# Fritzing sketch desenho esquematico (saved by Fritzing 0.9.3b)
breadboards: 1

parts:
  V- = Battery block 9V
  V+ = Battery block 9V
  R1 = Resistor [tolerance=±5% resistance=100k package=THT]
  R2 = Rotary Potentiometer (Small) [maximum_resistance=10kΩ package=THT]
  C1 = Electrolytic Capacitor [capacitance=10µF package="100 mil [THT, electrolytic]"]
  R3 = Resistor [tolerance=±5% resistance=100k package=THT]
  C2 = Ceramic Capacitor [capacitance=47nF package="100 mil [THT, multilayer]"]
  Componente1 = Arduino Uno (Rev3)
  R4 = Resistor [tolerance=±5% resistance=100k package=THT]
  TRS1 = Audio Jack (TRS) 3.5mm [package="PG203J [THT]"]
  LM_1 = DIP - 8 pins [chip_label="LM 741" package="DIP (Dual Inline) [THT]"]

nets:
  N1: V-.-, LM_1.pin4
  N2: V-.+, V+.-, R2.wiper, R3.Pin_0, C2.0, Componente1.GND, TRS1.Sleeve
  N3: V+.+, LM_1.pin7
  N4: R1.Pin_0, R2.leg1, LM_1.inverting_input
  N5: R1.Pin_1, C1.-, LM_1.pin6
  N6: C1.+, R3.Pin_1, C2.1, Componente1.A0, R4.Pin_0
  N7: Componente1.5V, R4.Pin_1
  N8: TRS1.Tip, LM_1.non-inverting_input

custom parts:
  DIP - 8 pins: A DIP stand-in part for whatever IC you want. With 8 pins on a 300mil dual inline package (DIP) footprint.
